// Logisim project TP 1 v.1 TRAN FLorian grp 4-2.circ as structural Verilog
module Half_adder (
  input  A,
  input  B,
  output out_3,
  output out_4
);

  xor xor_1 (out_3, A, B);
  and and_1 (out_4, A, B);
endmodule

module modified_adder (
  input  Cin,
  input  B,
  input  A,
  output R,
  output P,
  output G
);

  wire xor_1_out;

  xor xor_1 (xor_1_out, B, A);
  or or_1 (P, B, A);
  and and_1 (G, B, A);
  xor xor_2 (R, Cin, xor_1_out);
endmodule

module _4bit_adder (
  input  [3:0] in_1,
  input  [3:0] in_2,
  input  in_3,
  output [3:0] out_4,
  output out_5
);

  wire modified_adder_1_g, modified_adder_1_p, modified_adder_2_g, modified_adder_2_p, modified_adder_3_g,
       modified_adder_3_p, modified_adder_4_g, modified_adder_4_p, ucar_opti_1_c1, ucar_opti_1_c2,
       ucar_opti_1_c3;

  modified_adder modified_adder_1 (
    .Cin(in_3), .B(in_2[0]), .A(in_1[0]), .R(out_4[0]), .P(modified_adder_1_p), .G(modified_adder_1_g));
  UCAR_opti ucar_opti_1 (
    .Cin(in_3), .P0(modified_adder_1_p), .G0(modified_adder_1_g), .P1(modified_adder_2_p),
    .G1(modified_adder_2_g), .P2(modified_adder_3_p), .G2(modified_adder_3_g), .P3(modified_adder_4_p),
    .G3(modified_adder_4_g), .C1(ucar_opti_1_c1), .C2(ucar_opti_1_c2), .C3(ucar_opti_1_c3), .C4(out_5));
  modified_adder modified_adder_2 (
    .Cin(ucar_opti_1_c1), .B(in_2[1]), .A(in_1[1]), .R(out_4[1]), .P(modified_adder_2_p),
    .G(modified_adder_2_g));
  modified_adder modified_adder_3 (
    .Cin(ucar_opti_1_c2), .B(in_2[2]), .A(in_1[2]), .R(out_4[2]), .P(modified_adder_3_p),
    .G(modified_adder_3_g));
  modified_adder modified_adder_4 (
    .Cin(ucar_opti_1_c3), .B(in_2[3]), .A(in_1[3]), .R(out_4[3]), .P(modified_adder_4_p),
    .G(modified_adder_4_g));
endmodule

module UCAR (
  input  Cin,
  input  P0,
  input  G0,
  input  P0_2,
  input  G0_2,
  input  P0_3,
  input  G0_3,
  input  P0_4,
  input  G0_4,
  output Cout,
  output Cout_2,
  output Cout_3,
  output Cout_4
);

  wire and_1_out, and_2_out, and_3_out, and_4_out;

  and and_1 (and_1_out, Cin, P0);
  or or_1 (Cout, and_1_out, G0);
  and and_2 (and_2_out, Cout, P0_2);
  or or_2 (Cout_2, and_2_out, G0_2);
  and and_3 (and_3_out, Cout_2, P0_3);
  or or_3 (Cout_3, and_3_out, G0_3);
  and and_4 (and_4_out, Cout_3, P0_4);
  or or_4 (Cout_4, and_4_out, G0_4);
endmodule

module UCAR_opti (
  input  Cin,
  input  P0,
  input  G0,
  input  P1,
  input  G1,
  input  P2,
  input  G2,
  input  P3,
  input  G3,
  output C1,
  output C2,
  output C3,
  output C4
);

  wire and_1_out, and_2_out, and_3_out, and_4_out, and_5_out, and_6_out, and_7_out, and_8_out, and_9_out,
       and_10_out;

  and and_1 (and_1_out, Cin, P0);
  and and_2 (and_2_out, and_1_out, P1);
  and and_3 (and_3_out, P1, G0);
  and and_4 (and_4_out, and_2_out, P2);
  and and_5 (and_5_out, and_3_out, P2);
  and and_6 (and_6_out, P2, G1);
  and and_7 (and_7_out, and_4_out, P3);
  and and_8 (and_8_out, and_5_out, P3);
  and and_9 (and_9_out, and_6_out, P3);
  and and_10 (and_10_out, P3, G2);
  or or_1 (C1, and_1_out, G0);
  or or_2 (C2, and_2_out, and_3_out, G1);
  or or_3 (C3, and_4_out, and_5_out, and_6_out, G2);
  or or_4 (C4, and_7_out, and_8_out, and_9_out, and_10_out, G3);
endmodule
