// Logisim project TP 1 v.3 TRAN FLorian grp 4-2.circ as structural Verilog
module Half_adder (
  input  A,
  input  B,
  output R,
  output out_4
);

  xor xor_1 (R, A, B);
  and and_1 (out_4, A, B);

  // Notes on the sheet:
  //   Retenue
endmodule

module modified_adder (
  input  Cin,
  input  B,
  input  A,
  output R,
  output P,
  output G
);

  wire xor_1_out;

  xor xor_1 (xor_1_out, B, A);
  or or_1 (P, B, A);
  and and_1 (G, B, A);
  xor xor_2 (R, Cin, xor_1_out);
endmodule

module _4bit_adder (
  input  [3:0] in_1,
  input  [3:0] in_2,
  input  in_3,
  output [3:0] out_4,
  output out_5
);

  wire modified_adder_1_g, modified_adder_1_p, modified_adder_2_g, modified_adder_2_p, modified_adder_3_g,
       modified_adder_3_p, modified_adder_4_g, modified_adder_4_p, ucar_opti_1_c1, ucar_opti_1_c2,
       ucar_opti_1_c3;

  modified_adder modified_adder_1 (
    .Cin(in_3), .B(in_2[0]), .A(in_1[0]), .R(out_4[0]), .P(modified_adder_1_p), .G(modified_adder_1_g));
  UCAR_opti ucar_opti_1 (
    .Cin(in_3), .P0(modified_adder_1_p), .G0(modified_adder_1_g), .P1(modified_adder_3_p),
    .G1(modified_adder_3_g), .P2(modified_adder_2_p), .G2(modified_adder_2_g), .P3(modified_adder_4_p),
    .G3(modified_adder_4_g), .C1(ucar_opti_1_c1), .C2(ucar_opti_1_c2), .C3(ucar_opti_1_c3), .C4(out_5));
  modified_adder modified_adder_2 (
    .Cin(ucar_opti_1_c2), .B(in_2[2]), .A(in_1[2]), .R(out_4[2]), .P(modified_adder_2_p),
    .G(modified_adder_2_g));
  modified_adder modified_adder_3 (
    .Cin(ucar_opti_1_c1), .B(in_2[1]), .A(in_1[1]), .R(out_4[1]), .P(modified_adder_3_p),
    .G(modified_adder_3_g));
  modified_adder modified_adder_4 (
    .Cin(ucar_opti_1_c3), .B(in_2[3]), .A(in_1[3]), .R(out_4[3]), .P(modified_adder_4_p),
    .G(modified_adder_4_g));
endmodule

module UCAR (
  input  Cin,
  input  P0,
  input  G0,
  input  P0_2,
  input  G0_2,
  input  P0_3,
  input  G0_3,
  input  P0_4,
  input  G0_4,
  output Cout,
  output Cout_2,
  output Cout_3,
  output Cout_4
);

  wire and_1_out, and_2_out, and_3_out, and_4_out;

  and and_1 (and_1_out, Cin, P0);
  or or_1 (Cout, and_1_out, G0);
  and and_2 (and_2_out, Cout, P0_2);
  or or_2 (Cout_2, and_2_out, G0_2);
  and and_3 (and_3_out, Cout_2, P0_3);
  or or_3 (Cout_3, and_3_out, G0_3);
  and and_4 (and_4_out, Cout_3, P0_4);
  or or_4 (Cout_4, and_4_out, G0_4);
endmodule

module UCAR_opti (
  input  Cin,
  input  P0,
  input  G0,
  input  P1,
  input  G1,
  input  P2,
  input  G2,
  input  P3,
  input  G3,
  output C1,
  output C2,
  output C3,
  output C4
);

  wire and_1_out, and_2_out, and_3_out, and_4_out, and_5_out, and_6_out, and_7_out, and_8_out, and_9_out,
       and_10_out;

  and and_1 (and_1_out, Cin, P0);
  and and_2 (and_2_out, and_1_out, P1);
  and and_3 (and_3_out, P1, G0);
  and and_4 (and_4_out, and_2_out, P2);
  and and_5 (and_5_out, and_3_out, P2);
  and and_6 (and_6_out, P2, G1);
  and and_7 (and_7_out, and_4_out, P3);
  and and_8 (and_8_out, and_5_out, P3);
  and and_9 (and_9_out, and_6_out, P3);
  and and_10 (and_10_out, P3, G2);
  or or_1 (C1, and_1_out, G0);
  or or_2 (C2, and_2_out, and_3_out, G1);
  or or_3 (C3, and_4_out, and_5_out, and_6_out, G2);
  or or_4 (C4, and_7_out, and_8_out, and_9_out, and_10_out, G3);
endmodule

module _4bit_adder_super_p_g (
  input  [3:0] in_1,
  input  [3:0] in_2,
  input  in_3,
  output [3:0] out_4,
  output out_5,
  output out_6
);

  wire modified_adder_1_g, modified_adder_1_p, modified_adder_2_g, modified_adder_2_p, modified_adder_3_g,
       modified_adder_3_p, modified_adder_4_g, modified_adder_4_p, ucar_super_p_g_1_c1, ucar_super_p_g_1_c2,
       ucar_super_p_g_1_c3;

  modified_adder modified_adder_1 (
    .Cin(in_3), .B(in_2[0]), .A(in_1[0]), .R(out_4[0]), .P(modified_adder_1_p), .G(modified_adder_1_g));
  UCAR_super_p_g ucar_super_p_g_1 (
    .Cin(in_3), .P0(modified_adder_1_p), .G0(modified_adder_1_g), .P1(modified_adder_3_p),
    .G1(modified_adder_3_g), .P2(modified_adder_2_p), .G2(modified_adder_2_g), .G3(modified_adder_4_g),
    .C1(ucar_super_p_g_1_c1), .C2(ucar_super_p_g_1_c2), .C3(ucar_super_p_g_1_c3), .P3(modified_adder_4_p),
    .SP(out_5), .SG(out_6));
  modified_adder modified_adder_2 (
    .Cin(ucar_super_p_g_1_c2), .B(in_2[2]), .A(in_1[2]), .R(out_4[2]), .P(modified_adder_2_p),
    .G(modified_adder_2_g));
  modified_adder modified_adder_3 (
    .Cin(ucar_super_p_g_1_c1), .B(in_2[1]), .A(in_1[1]), .R(out_4[1]), .P(modified_adder_3_p),
    .G(modified_adder_3_g));
  modified_adder modified_adder_4 (
    .Cin(ucar_super_p_g_1_c3), .B(in_2[3]), .A(in_1[3]), .R(out_4[3]), .P(modified_adder_4_p),
    .G(modified_adder_4_g));
endmodule

module _16bit_adder (
  input  [15:0] in_1,
  input  [15:0] in_2,
  input  in_3,
  output [15:0] out_4,
  output Cout
);

  wire n4bit_adder_super_p_g_1_out_5, n4bit_adder_super_p_g_1_out_6, n4bit_adder_super_p_g_2_out_5,
       n4bit_adder_super_p_g_2_out_6, n4bit_adder_super_p_g_3_out_5, n4bit_adder_super_p_g_3_out_6,
       n4bit_adder_super_p_g_4_out_5, n4bit_adder_super_p_g_4_out_6, ucar_super_p_g_1_c1,
       ucar_super_p_g_1_c2, ucar_super_p_g_1_c3, ucar_super_p_g_1_sg, ucar_super_p_g_1_sp;

  _4bit_adder_super_p_g u_4bit_adder_super_p_g_1 (
    .in_1(in_2[3:0]), .in_2(in_1[3:0]), .in_3(in_3), .out_4(out_4[3:0]),
    .out_5(n4bit_adder_super_p_g_1_out_5), .out_6(n4bit_adder_super_p_g_1_out_6));
  _4bit_adder_super_p_g u_4bit_adder_super_p_g_2 (
    .in_1(in_2[7:4]), .in_2(in_1[7:4]), .in_3(ucar_super_p_g_1_c1), .out_4(out_4[7:4]),
    .out_5(n4bit_adder_super_p_g_2_out_5), .out_6(n4bit_adder_super_p_g_2_out_6));
  UCAR_super_p_g ucar_super_p_g_1 (
    .Cin(in_3), .P0(n4bit_adder_super_p_g_1_out_5), .G0(n4bit_adder_super_p_g_1_out_6),
    .P1(n4bit_adder_super_p_g_2_out_5), .G1(n4bit_adder_super_p_g_2_out_6),
    .P2(n4bit_adder_super_p_g_3_out_5), .G2(n4bit_adder_super_p_g_3_out_6),
    .G3(n4bit_adder_super_p_g_4_out_6), .C1(ucar_super_p_g_1_c1), .C2(ucar_super_p_g_1_c2),
    .C3(ucar_super_p_g_1_c3), .P3(n4bit_adder_super_p_g_4_out_5), .SP(ucar_super_p_g_1_sp),
    .SG(ucar_super_p_g_1_sg));
  _4bit_adder_super_p_g u_4bit_adder_super_p_g_3 (
    .in_1(in_2[11:8]), .in_2(in_1[11:8]), .in_3(ucar_super_p_g_1_c2), .out_4(out_4[11:8]),
    .out_5(n4bit_adder_super_p_g_3_out_5), .out_6(n4bit_adder_super_p_g_3_out_6));
  _4bit_adder_super_p_g u_4bit_adder_super_p_g_4 (
    .in_1(in_2[15:12]), .in_2(in_1[15:12]), .in_3(ucar_super_p_g_1_c3), .out_4(out_4[15:12]),
    .out_5(n4bit_adder_super_p_g_4_out_5), .out_6(n4bit_adder_super_p_g_4_out_6));
  carry carry_1 (.in_1(ucar_super_p_g_1_sg), .in_2(ucar_super_p_g_1_sp), .in_3(in_3), .out_4(Cout));
endmodule

module UCAR_super_p_g (
  input  Cin,
  input  P0,
  input  G0,
  input  P1,
  input  G1,
  input  P2,
  input  G2,
  input  P3,
  input  G3,
  output C1,
  output C2,
  output C3,
  output SP,
  output SG
);

  wire and_1_out, and_2_out, and_3_out, and_4_out, and_5_out, and_6_out;

  and and_1 (and_1_out, Cin, P0);
  and and_2 (and_2_out, and_1_out, P1);
  SG sg_1 (.G0(G0), .G1(G1), .G2(G2), .G3(G3), .P1(P1), .P2(P2), .P3(P3), .SG(SG));
  and and_3 (and_3_out, P1, G0);
  and and_4 (and_4_out, and_2_out, P2);
  and and_5 (and_5_out, and_3_out, P2);
  and and_6 (and_6_out, P2, G1);
  or or_1 (C1, and_1_out, G0);
  or or_2 (C2, and_2_out, and_3_out, G1);
  or or_3 (C3, and_4_out, and_5_out, and_6_out, G2);
  and and_7 (SP, P0, P1, P2, P3);
endmodule

module SG (
  input  P1,
  input  P2,
  input  P3,
  input  G0,
  input  G1,
  input  G2,
  input  G3,
  output SG
);

  wire and_1_out, and_2_out, and_3_out, and_4_out;

  and and_1 (and_1_out, P3, P2, P1);
  and and_2 (and_2_out, P3, G2);
  and and_3 (and_3_out, and_1_out, G0);
  and and_4 (and_4_out, and_1_out, G1);
  or or_1 (SG, and_3_out, and_4_out, and_2_out, G3);
endmodule

module _16bit_soustract (
  input  [15:0] in_1,
  input  [15:0] in_2,
  output [15:0] out_3,
  output cout
);

  wire n4bit_adder_super_p_g_1_out_5, n4bit_adder_super_p_g_1_out_6, n4bit_adder_super_p_g_2_out_5,
       n4bit_adder_super_p_g_2_out_6, n4bit_adder_super_p_g_3_out_5, n4bit_adder_super_p_g_3_out_6,
       n4bit_adder_super_p_g_4_out_5, n4bit_adder_super_p_g_4_out_6, ucar_super_p_g_1_c1,
       ucar_super_p_g_1_c2, ucar_super_p_g_1_c3, ucar_super_p_g_1_sg, ucar_super_p_g_1_sp;
  wire [15:0] not_1_out;

  assign not_1_out = ~in_2;  // NOT_Gate not_1, 16 bits wide
  _4bit_adder_super_p_g u_4bit_adder_super_p_g_1 (
    .in_1(not_1_out[3:0]), .in_2(in_1[3:0]), .in_3(1'b1), .out_4(out_3[3:0]),
    .out_5(n4bit_adder_super_p_g_1_out_5), .out_6(n4bit_adder_super_p_g_1_out_6));
  _4bit_adder_super_p_g u_4bit_adder_super_p_g_2 (
    .in_1(not_1_out[7:4]), .in_2(in_1[7:4]), .in_3(ucar_super_p_g_1_c1), .out_4(out_3[7:4]),
    .out_5(n4bit_adder_super_p_g_2_out_5), .out_6(n4bit_adder_super_p_g_2_out_6));
  UCAR_super_p_g ucar_super_p_g_1 (
    .Cin(1'b1), .P0(n4bit_adder_super_p_g_1_out_5), .G0(n4bit_adder_super_p_g_1_out_6),
    .P1(n4bit_adder_super_p_g_2_out_5), .G1(n4bit_adder_super_p_g_2_out_6),
    .P2(n4bit_adder_super_p_g_3_out_5), .G2(n4bit_adder_super_p_g_3_out_6),
    .G3(n4bit_adder_super_p_g_4_out_6), .C1(ucar_super_p_g_1_c1), .C2(ucar_super_p_g_1_c2),
    .C3(ucar_super_p_g_1_c3), .P3(n4bit_adder_super_p_g_4_out_5), .SP(ucar_super_p_g_1_sp),
    .SG(ucar_super_p_g_1_sg));
  _4bit_adder_super_p_g u_4bit_adder_super_p_g_3 (
    .in_1(not_1_out[11:8]), .in_2(in_1[11:8]), .in_3(ucar_super_p_g_1_c2), .out_4(out_3[11:8]),
    .out_5(n4bit_adder_super_p_g_3_out_5), .out_6(n4bit_adder_super_p_g_3_out_6));
  _4bit_adder_super_p_g u_4bit_adder_super_p_g_4 (
    .in_1(not_1_out[15:12]), .in_2(in_1[15:12]), .in_3(ucar_super_p_g_1_c3), .out_4(out_3[15:12]),
    .out_5(n4bit_adder_super_p_g_4_out_5), .out_6(n4bit_adder_super_p_g_4_out_6));
  carry carry_1 (.in_1(ucar_super_p_g_1_sg), .in_2(ucar_super_p_g_1_sp), .in_3(1'b1), .out_4(cout));
endmodule

module Multiplex (
  input  [15:0] in_1,
  input  [15:0] in_2,
  input  in_3,
  input  [2:0] in_4,
  output [15:0] out_5,
  output N,
  output Z,
  output C,
  output V
);

  wire and_2_out;
  wire [15:0] and_1_out, n16bit_adder_1_out_4, n16bit_soustract_1_p4, not_1_out, shifter_1_out,
       shifter_2_out, xor_1_out;

  assign xor_1_out = in_1 ^ in_2;  // XOR_Gate xor_1, 16 bits wide
  Shifter #(.width(16)) shifter_1 (.in(in_1), .\dist (4'b0001), .out(shifter_1_out));
  Shifter #(.width(16), .shift("ar")) shifter_2 (.in(in_2), .\dist (4'b0001), .out(shifter_2_out));
  assign not_1_out = ~in_1;  // NOT_Gate not_1, 16 bits wide
  assign and_1_out = in_1 & in_1;  // AND_Gate and_1, 16 bits wide
  _16bit_adder u_16bit_adder_1 (.in_1(in_1), .in_2(in_2), .in_3(in_3), .out_4(n16bit_adder_1_out_4), .Cout(C));
  // _16bit_soustract 16bit_soustract_1: pin names not known; wires that end beside it: in_1, in_2, in_3, n16bit_soustract_1_p4
  Multiplexer #(.select(3), .width(16), .enable("false")) multiplexer_1 (
    .in0(n16bit_adder_1_out_4), .in1(n16bit_soustract_1_p4), .in2(not_1_out), .in3(and_1_out),
    .in4(n16bit_adder_1_out_4), .in5(xor_1_out), .in6(shifter_1_out), .in7(shifter_2_out),
    .out({N, out_5[14:0]}), .sel(in_4));
  nor nor_1 (Z, N, out_5[14], out_5[13], out_5[12], out_5[11], out_5[10], out_5[9], out_5[8], out_5[7], out_5[6], out_5[5], out_5[4], out_5[3], out_5[2], out_5[1], out_5[0]);
  and and_2 (and_2_out, in_1[15], in_2[15]);
  xor xor_2 (V, and_2_out, N);

  assign out_5[15] = N;
endmodule

module carry (
  input  in_1,
  input  in_2,
  input  in_3,
  output out_4
);

  wire and_1_out;

  and and_1 (and_1_out, in_1, in_2);
  or or_1 (out_4, and_1_out, in_3);
endmodule
